// Digital circuit 1.dig as structural Verilog
module _1 (
  input  P2,
  input  S,
  input  P1,
  output V,
  output R
);

  wire and_1_out, and_2_out, and_3_out, and_4_out, and_5_out, not_1_out, not_2_out, not_3_out, not_4_out,
       not_5_out;

  not not_1 (not_1_out, P1);
  not not_2 (not_2_out, P2);
  and and_1 (and_1_out, P1, not_2_out);
  and and_2 (and_2_out, P2, S);
  and and_3 (and_3_out, not_1_out, P2);
  or or_1 (V, and_1_out, and_2_out, and_3_out);
  not not_3 (not_3_out, not_1_out);
  not not_4 (not_4_out, P2);
  not not_5 (not_5_out, S);
  and and_4 (and_4_out, not_3_out, not_4_out);
  and and_5 (and_5_out, P1, P2, not_5_out);
  or or_2 (R, and_4_out, and_5_out);
endmodule
