// Digital circuit 3.dig as structural Verilog
module _3 (
  input  N1,
  input  N2,
  input  N3,
  input  N4,
  input  N0,
  input  M,
  input  N6,
  input  N7,
  input  N8,
  input  N9,
  input  N5,
  input  M_2,
  output Y,
  output Y_2
);

  wire and_1_out, and_2_out, and_3_out, and_4_out, decoder_1_out_20, decoder_1_out_21, decoder_1_out_22,
       decoder_1_out_23, decoder_1_out_30, not_1_out, not_2_out, not_3_out, not_4_out, or_1_out;

  Decoder #(.Selector_Bits(5)) decoder_1 (
    .sel({N0, N1, N2, N3, N4}), .out_20(decoder_1_out_20), .out_21(decoder_1_out_21),
    .out_22(decoder_1_out_22), .out_23(decoder_1_out_23), .out_30(decoder_1_out_30));  // open: out_0, out_1, out_2, out_3, out_4, out_5, out_6, out_7, out_8, out_9, out_10, out_11, out_12, out_13, out_14, out_15, out_16, out_17, out_18, out_19, out_24, out_25, out_26, out_27, out_28, out_29, out_31
  not not_1 (not_1_out, M);
  or or_1 (or_1_out, decoder_1_out_20, decoder_1_out_21, decoder_1_out_22, decoder_1_out_23);
  and and_1 (and_1_out, decoder_1_out_30, not_1_out);
  and and_2 (and_2_out, or_1_out, M);
  xor xor_1 (Y, and_2_out, and_1_out);
  not not_2 (not_2_out, N9);
  not not_3 (not_3_out, M_2);
  not not_4 (not_4_out, N6);
  and and_3 (and_3_out, not_3_out, not_2_out, N8, N7, N6, N5);
  and and_4 (and_4_out, M_2, N7, not_4_out, N5);
  xor xor_2 (Y_2, and_3_out, and_4_out);
endmodule
