// Digital circuit Esercizio1.dig as structural Verilog
module Esercizio1 (
  input  x2,
  input  x1,
  input  x0,
  input  x3,
  input  x4,
  input  x1_2,
  input  x3_2,
  input  x4_2,
  input  x0_2,
  input  x2_2,
  input  x4_3,
  input  x3_3,
  input  x1_3,
  input  x0_3,
  input  x2_3,
  output U,
  output U_2,
  output U_3
);

  wire and_1_out, and_2_out, and_3_out, nand_1_out, nand_2_out, nand_3_out, nand_4_out, nand_5_out,
       nand_6_out, not_1_out, not_2_out, not_3_out, not_4_out, not_5_out, not_6_out, not_7_out, not_8_out,
       not_9_out, not_10_out, not_11_out, or_1_out, or_2_out, or_3_out, xor_1_out;

  not not_1 (not_1_out, x2);
  and and_1 (and_1_out, x0_3, x2_3);
  nand nand_1 (nand_1_out, x4, x3, not_1_out);
  not not_2 (not_2_out, x2);
  not not_3 (not_3_out, x4);
  not not_4 (not_4_out, x0);
  not not_5 (not_5_out, x3);
  not not_6 (not_6_out, x1);
  not not_7 (not_7_out, x0);
  xor xor_1 (xor_1_out, x0_3, x1_3, x2_3);
  nand nand_2 (nand_2_out, x4, not_2_out);
  nand nand_3 (nand_3_out, not_3_out, x3, x0);
  nand nand_4 (nand_4_out, x3, x1, not_4_out);
  nand nand_5 (nand_5_out, not_5_out, x2, x1, x0);
  nand nand_6 (nand_6_out, x2, not_6_out, not_7_out);
  not not_8 (not_8_out, x0_3);
  not not_9 (not_9_out, x1_3);
  not not_10 (not_10_out, x2_3);
  not not_11 (not_11_out, and_1_out);
  and and_2 (and_2_out, x0_3, x1_3, x2_3);
  and and_3 (and_3_out, not_8_out, not_9_out, x2_3);
  or or_1 (or_1_out, x0_3, x1_3, x1_3);
  or or_2 (or_2_out, xor_1_out, not_10_out);
  or or_3 (or_3_out, and_2_out, and_3_out);
  nand nand_7 (U, nand_1_out, nand_2_out, nand_3_out, nand_4_out, nand_5_out, nand_6_out);
  Multiplexer #(.Selector_Bits(2)) multiplexer_1 (
    .sel({x4_3, x3_3}), .in_0(or_3_out), .in_1(or_1_out), .in_2(or_2_out), .in_3(not_11_out), .out(U_3));
  Multiplexer #(.Selector_Bits(5)) multiplexer_2 (
    .sel({x4_2, x3_2, x2_2, x1_2, x0_2}), .in_0(1'b0), .in_1(1'b0), .in_2(1'b0), .in_3(1'b0), .in_4(1'b1),
    .in_5(1'b0), .in_6(1'b0), .in_7(1'b1), .in_8(1'b0), .in_9(1'b1), .in_10(1'b1), .in_11(1'b1),
    .in_12(1'b1), .in_13(1'b1), .in_14(1'b1), .in_15(1'b1), .in_16(1'b1), .in_17(1'b1), .in_18(1'b1),
    .in_19(1'b1), .in_20(1'b1), .in_21(1'b0), .in_22(1'b0), .in_23(1'b1), .in_24(1'b1), .in_25(1'b1),
    .in_26(1'b1), .in_27(1'b1), .in_28(1'b1), .in_29(1'b1), .in_30(1'b1), .in_31(1'b0), .out(U_2));
endmodule
