// Digital circuit Esercizio2_6.dig as structural Verilog
module Esercizio2_6 (
  input  a1,
  input  a2,
  input  a3,
  input  a4,
  input  a5,
  input  b1,
  input  b2,
  input  b3,
  input  b4,
  input  b5,
  input  x2,
  input  x1,
  input  x3,
  input  F1,
  input  F2,
  input  F3,
  input  F4,
  input  F5,
  input  F6,
  input  F7,
  input  F8,
  output z1,
  output z2,
  output z3,
  output z4,
  output z5,
  output CF,
  output z
);

  wire add_1_c_o, add_2_c_o, add_3_c_o, add_4_c_o, not_1_out, not_2_out, not_3_out, not_4_out, not_5_out,
       not_6_out, not_7_out, not_8_out, not_9_out, not_10_out, not_11_out, not_12_out, or_1_out, or_2_out,
       or_3_out, or_4_out, or_5_out, or_6_out, or_7_out, or_8_out;

  not not_1 (not_1_out, x3);
  not not_2 (not_2_out, x1);
  not not_3 (not_3_out, x1);
  not not_4 (not_4_out, x3);
  not not_5 (not_5_out, x2);
  not not_6 (not_6_out, x2);
  not not_7 (not_7_out, x3);
  not not_8 (not_8_out, x1);
  not not_9 (not_9_out, x2);
  not not_10 (not_10_out, x1);
  not not_11 (not_11_out, x2);
  not not_12 (not_12_out, x3);
  or or_1 (or_1_out, x1, x2, x3, F1);
  or or_2 (or_2_out, x1, x2, not_1_out, F2);
  or or_3 (or_3_out, not_2_out, x2, x3, F3);
  or or_4 (or_4_out, not_3_out, x2, not_4_out, F4);
  or or_5 (or_5_out, x1, not_5_out, x3, F5);
  or or_6 (or_6_out, x1, not_6_out, not_7_out, F6);
  or or_7 (or_7_out, not_8_out, not_9_out, x3, F7);
  or or_8 (or_8_out, not_10_out, not_11_out, not_12_out, F8);
  and and_1 (z, or_1_out, or_2_out, or_3_out, or_4_out, or_5_out, or_6_out, or_7_out, or_8_out);
  Add add_1 (.a(a1), .b(b1), .c_i(1'b0), .s(z1), .c_o(add_1_c_o));
  Add add_2 (.a(a2), .b(b2), .c_i(add_1_c_o), .s(z2), .c_o(add_2_c_o));
  Add add_3 (.a(a3), .b(b3), .c_i(add_2_c_o), .s(z3), .c_o(add_3_c_o));
  Add add_4 (.a(a4), .b(b4), .c_i(add_3_c_o), .s(z4), .c_o(add_4_c_o));
  Add add_5 (.a(a5), .b(b5), .c_i(add_4_c_o), .s(z5), .c_o(CF));
endmodule
