// Digital circuit Esercizio3.dig as structural Verilog
module Esercizio3 (
  input  a,
  input  b,
  input  c,
  input  d,
  output U
);

  wire nor_1_out, nor_2_out, nor_3_out, nor_4_out, nor_5_out, nor_6_out, nor_7_out, not_1_out, not_2_out,
       not_3_out;

  not not_1 (not_1_out, c);
  nor nor_1 (nor_1_out, a, b);
  nor nor_2 (nor_2_out, b, not_1_out);
  nor nor_3 (nor_3_out, c, d);
  not not_2 (not_2_out, d);
  nor nor_4 (nor_4_out, a, not_2_out);
  nor nor_5 (nor_5_out, not_3_out, nor_2_out);
  not not_3 (not_3_out, a);
  nor nor_6 (nor_6_out, nor_1_out, nor_3_out);
  nor nor_7 (nor_7_out, nor_5_out, nor_6_out);
  nor nor_8 (U, nor_4_out, nor_7_out);
endmodule
