// Digital circuit 2.dig as structural Verilog
module _2 (
  input  A,
  input  B,
  input  C,
  input  D,
  input  I,
  input  A_2,
  input  B_2,
  input  C_2,
  input  D_2,
  input  I_2,
  input  A_3,
  input  C_3,
  input  I_3,
  input  A_4,
  input  C_4,
  input  I_4,
  input  in_27,
  input  in_28,
  input  in_29,
  input  in_30,
  input  in_31,
  input  in_32,
  input  in_33,
  input  in_34,
  input  in_35,
  input  in_36,
  input  in_37,
  input  in_38,
  input  in_39,
  input  in_40,
  input  in_41,
  input  in_42,
  input  in_43,
  input  in_44,
  input  in_45,
  input  in_46,
  input  in_47,
  input  in_48,
  input  in_49,
  input  in_50,
  input  in_51,
  input  in_52,
  input  in_53,
  input  in_54,
  input  in_55,
  input  in_56,
  input  in_57,
  input  in_58,
  input  A_5,
  input  B_3,
  input  C_5,
  input  D_3,
  input  I_5,
  input  in_65,
  input  in_66,
  input  in_67,
  input  in_68,
  input  in_69,
  input  in_70,
  input  in_71,
  input  in_72,
  input  A_6,
  input  B_4,
  input  C_6,
  input  D_4,
  input  I_6,
  output OnA,
  output OnB,
  output OnC,
  output OnD,
  output OnA_2,
  output OnB_2,
  output OnC_2,
  output OnD_2,
  output OnC_3,
  output OnC_4,
  output OnA_3,
  output OnC_5
);

  wire and_1_out, and_2_out, and_3_out, and_4_out, and_5_out, and_6_out, and_7_out, and_8_out,
       multiplexer_1_out, multiplexer_2_out, nand_1_out, nand_2_out, nor_1_out, nor_2_out, nor_3_out,
       not_1_out, not_2_out, not_3_out, not_4_out, not_5_out, not_6_out, not_7_out, not_8_out, not_9_out,
       not_10_out, not_11_out, not_12_out, not_13_out, not_14_out, not_15_out, not_16_out, not_17_out,
       not_18_out, not_19_out, not_20_out, not_21_out, not_22_out, not_23_out, not_24_out, not_25_out,
       not_26_out, not_27_out, not_28_out, not_29_out, not_30_out, not_31_out, not_32_out, not_33_out,
       not_34_out, not_35_out, not_36_out, not_37_out, not_38_out, not_39_out, not_40_out, not_41_out,
       not_42_out, not_43_out, not_44_out, not_45_out, not_46_out, not_47_out, not_48_out, not_49_out,
       not_50_out, not_51_out, not_52_out, or_5_out, or_6_out, or_7_out, or_8_out, or_9_out, or_10_out,
       or_11_out, or_12_out, or_13_out;

  not not_1 (not_1_out, A);
  not not_2 (not_2_out, I);
  not not_3 (not_3_out, C);
  not not_4 (not_4_out, I);
  not not_5 (not_5_out, A);
  not not_6 (not_6_out, I);
  not not_7 (not_7_out, B);
  not not_8 (not_8_out, I);
  not not_9 (not_9_out, D);
  and and_1 (and_1_out, A, not_4_out);
  and and_2 (and_2_out, not_5_out, I);
  and and_3 (and_3_out, B, not_6_out);
  and and_4 (and_4_out, not_7_out, I);
  and and_5 (and_5_out, not_1_out, C, not_2_out);
  and and_6 (and_6_out, A, not_3_out, I);
  and and_7 (and_7_out, D, not_8_out);
  and and_8 (and_8_out, not_9_out, I);
  or or_1 (OnA, and_1_out, and_2_out);
  or or_2 (OnB, and_3_out, and_4_out);
  or or_3 (OnC, and_5_out, and_6_out);
  or or_4 (OnD, and_7_out, and_8_out);
  not not_10 (not_10_out, A_2);
  not not_11 (not_11_out, I_2);
  not not_12 (not_12_out, B_2);
  not not_13 (not_13_out, I_2);
  not not_14 (not_14_out, I_2);
  not not_15 (not_15_out, A_2);
  not not_16 (not_16_out, C_2);
  not not_17 (not_17_out, D_2);
  not not_18 (not_18_out, I_2);
  or or_5 (or_5_out, A_2, I_2);
  or or_6 (or_6_out, not_10_out, not_11_out);
  or or_7 (or_7_out, B_2, B_2);
  or or_8 (or_8_out, not_12_out, not_13_out);
  or or_9 (or_9_out, A_2, not_14_out);
  or or_10 (or_10_out, not_15_out, not_16_out);
  or or_11 (or_11_out, C_2, I_2);
  or or_12 (or_12_out, D_2, D_2);
  or or_13 (or_13_out, not_17_out, not_18_out);
  and and_9 (OnA_2, or_5_out, or_6_out);
  and and_10 (OnB_2, or_7_out, or_8_out);
  and and_11 (OnC_2, or_9_out, or_10_out, or_11_out);
  and and_12 (OnD_2, or_12_out, or_13_out);
  not not_19 (not_19_out, A_3);
  not not_20 (not_20_out, I_3);
  not not_21 (not_21_out, C_3);
  not not_22 (not_22_out, A_4);
  not not_23 (not_23_out, C_4);
  not not_24 (not_24_out, I_4);
  nand nand_1 (nand_1_out, not_19_out, C_3, not_20_out);
  nand nand_2 (nand_2_out, A_3, not_21_out, I_3);
  nor nor_1 (nor_1_out, not_22_out, not_23_out);
  nor nor_2 (nor_2_out, A_4, not_24_out);
  nor nor_3 (nor_3_out, C_4, I_4);
  nand nand_3 (OnC_3, nand_1_out, nand_2_out);
  nor nor_4 (OnC_4, nor_1_out, nor_2_out, nor_3_out);
  not not_25 (not_25_out, in_27);
  not not_26 (not_26_out, in_28);
  not not_27 (not_27_out, in_29);
  not not_28 (not_28_out, in_30);
  not not_29 (not_29_out, in_31);
  not not_30 (not_30_out, in_32);
  not not_31 (not_31_out, in_33);
  not not_32 (not_32_out, in_34);
  not not_33 (not_33_out, in_51);
  not not_34 (not_34_out, in_52);
  not not_35 (not_35_out, in_53);
  not not_36 (not_36_out, in_54);
  not not_37 (not_37_out, in_55);
  not not_38 (not_38_out, in_56);
  not not_39 (not_39_out, in_57);
  not not_40 (not_40_out, in_58);
  Multiplexer #(.Selector_Bits(4)) multiplexer_1 (
    .sel({D_3, C_5, B_3, A_5}), .in_0(not_25_out), .in_1(not_26_out), .in_2(not_27_out), .in_3(not_28_out),
    .in_4(not_29_out), .in_5(not_30_out), .in_6(not_31_out), .in_7(not_32_out), .in_8(in_35), .in_9(in_36),
    .in_10(in_37), .in_11(in_38), .in_12(in_39), .in_13(in_40), .in_14(in_41), .in_15(in_42),
    .out(multiplexer_1_out));
  Multiplexer #(.Selector_Bits(4)) multiplexer_2 (
    .sel({D_3, C_5, B_3, A_5}), .in_0(in_43), .in_1(in_44), .in_2(in_45), .in_3(in_46), .in_4(in_47),
    .in_5(in_48), .in_6(in_49), .in_7(in_50), .in_8(not_33_out), .in_9(not_34_out), .in_10(not_35_out),
    .in_11(not_36_out), .in_12(not_37_out), .in_13(not_38_out), .in_14(not_39_out), .in_15(not_40_out),
    .out(multiplexer_2_out));
  Multiplexer multiplexer_3 (.sel(I_5), .in_0(multiplexer_1_out), .in_1(multiplexer_2_out), .out(OnA_3));
  not not_41 (not_41_out, in_65);
  not not_42 (not_42_out, in_66);
  not not_43 (not_43_out, I_6);
  not not_44 (not_44_out, I_6);
  not not_45 (not_45_out, in_67);
  not not_46 (not_46_out, in_68);
  not not_47 (not_47_out, I_6);
  not not_48 (not_48_out, I_6);
  not not_49 (not_49_out, in_69);
  not not_50 (not_50_out, in_70);
  not not_51 (not_51_out, in_71);
  not not_52 (not_52_out, in_72);
  Multiplexer #(.Selector_Bits(4)) multiplexer_4 (
    .sel({D_4, C_6, B_4, A_6}), .in_0(not_41_out), .in_1(not_42_out), .in_2(not_43_out), .in_3(not_44_out),
    .in_4(not_45_out), .in_5(not_46_out), .in_6(not_47_out), .in_7(not_48_out), .in_8(I_6), .in_9(I_6),
    .in_10(not_49_out), .in_11(not_50_out), .in_12(I_6), .in_13(I_6), .in_14(not_51_out), .in_15(not_52_out),
    .out(OnC_5));
endmodule
